# Fritzing sketch Esquema Estufa Inteligente (saved by Fritzing 0.9.3b)
breadboards: 1

parts:
  DHT11 = DHT11 Humitidy and Temperature Sensor
  Temperarura_e_Umidade_A_prova_d'agua = DS18B20 1-Wire Temperature Sensor [part_number=DS18B20]
  FC_-_28_Umidade_do_Solo = FC-28 Soil Hygrometer Module
  R1 = Resistor [tolerance=±5% resistance=4.7k package="0402 [SMD]"]
  U1 = 2-Channel 5v Relay Shield [package=relay-2ch5v10a]
  LED2 = smd LED [color="Green (565nm)" package="1206 [SMD]"]
  LED3 = smd LED [color="Red (633nm)" package="1206 [SMD]"]
  LED4 = smd LED [color="Yellow (592nm)" package="1206 [SMD]"]
  R2 = Resistor [tolerance=±5% resistance=300 package="2010 [SMD]"]
  R3 = Resistor [tolerance=±5% resistance=300 package="2010 [SMD]"]
  R4 = Resistor [tolerance=±5% resistance=300 package="2010 [SMD]"]
  Componente1 = Arduino Uno (Rev3) - ICSP
  F1 = Fan - Ventilador [package=THT]  # not connected
  F2 = Fan - Ventilador [package=THT]

nets:
  VDD: DHT11.VDD, Temperarura_e_Umidade_A_prova_d'agua.VDD, FC_-_28_Umidade_do_Solo.VCC, R1.Pin_1, U1.VCC, U1.IN2, F2.5V
  GND: DHT11.GND, Temperarura_e_Umidade_A_prova_d'agua.GND, FC_-_28_Umidade_do_Solo.GND, U1.GND, LED2.cathode, LED3.cathode, LED4.cathode
  N1: Temperarura_e_Umidade_A_prova_d'agua.DQ, R1.Pin_0, Componente1.D3_PWM
  N2: FC_-_28_Umidade_do_Solo.AO, Componente1.A1
  N3: U1.IN1, Componente1.D5_PWM
  N4: LED2.anode, R2.Pin_0
  N5: LED3.anode, R4.Pin_0
  N6: LED4.anode, R3.Pin_0
  N7: R2.Pin_1, Componente1.D13/SCK
  N8: R3.Pin_1, Componente1.ICSP_MISO, Componente1.D12/MISO
  N9: R4.Pin_1, Componente1.D7

custom parts:
  DHT11 Humitidy and Temperature Sensor: DHT11 Humidity and Temperature Sensor
  FC-28 Soil Hygrometer Module: The FC-28 is a soil hygrometer module that uses the Texas Instruments LM393 comparator chip to provide an analog measurement of soil humidity. The digital output is high when soil moisture is over a certain threshold, as determined by adjusting the potentiometer.
  2-Channel 5v Relay Shield: 2 Channel 5v Relay Shield w. 2x SPD-06VDC-SD-C
  Fan - Ventilador: Ventilador de 2 pines, se encuentra comunmente en computadoras de escritorio
